# Fritzing sketch RX_Motor (saved by Fritzing 0.9.2b)
breadboards: 1

parts:
  A7105 = mystery part, 14 pins [chip_label=A7105]
  IC1 = L293D [package=THT]
  M2 = DC Motor
  M1 = DC Motor
  LED1 = LED - 5mm [color="Red (633nm)" package="5 mm [THT]"]
  SERVO = single row smd male pin header, 3 pins [form="♂ (male)"]
  Composants1 = Arduino Pro Mini v13
  Select_1-2S = male pin header, 3 pins [form="♂ (male)"]
  Jump = female pin header, 2 pins [form="♀ (female)"]
  Accus_2S = female pin header, 2 pins [form="♀ (female)"]
  BAT_2S = 4 x AAA Battery Mount
  BAT_1S = 4 x AAA Battery Mount
  R1 = Resistor [tolerance=±5% resistance=470 package=THT]
  R2 = Resistor [tolerance=±5% resistance=470 package=THT]
  R3 = Resistor [tolerance=±5% resistance=470 package=THT]
  R4 = Resistor [tolerance=±5% resistance=470 package=THT]
  LED2 = LED - 5mm [color="Red (633nm)" package="5 mm [THT]"]
  LED3 = LED - 5mm [color="White (4500K)" package="5 mm [THT]"]
  LED4 = LED - 5mm [color="Green (560nm)" package="5 mm [THT]"]
  LED5 = LED - 5mm [color="White (4500K)" package="5 mm [THT]"]
  R5 = Resistor [tolerance=±5% resistance=8.2k package=THT]
  R6 = Resistor [tolerance=±5% resistance=1k package=THT]
  U1 = Voltage Regulator - 3.3V [package="TO220 [THT]"]

nets:
  FLYSKY: A7105.pin2
  N1: A7105.pin8, Composants1.D5_PWM
  N2: A7105.pin9, Composants1.D4
  N3: A7105.pin10, Composants1.D2
  GND: A7105.pin12, IC1.0V, LED1.cathode, SERVO.pin1, Composants1.GND, Select_1-2S.pin1, BAT_1S.-, LED2.cathode, LED3.cathode, LED4.cathode, LED5.cathode, R6.Pin_1, U1.GND
  3.3V: A7105.pin13, IC1.+V, SERVO.pin2, Composants1.VCC, Select_1-2S.pin3, BAT_1S.+, U1.output_voltage
  N4: IC1.Enable_1, Composants1.D3_PWM
  N5: IC1.In_1, Composants1.D7
  N6: IC1.Out_1_(_Controlled_by_Enable_1_), M1.pin_1
  N7: IC1.Out_2_(_Controlled_by_Enable_1_), M1.pin_2
  N8: IC1.In_2, Composants1.D6_PWM
  N9: IC1.+Vmotor, Select_1-2S.pin2, R5.Pin_0, U1.input_voltage
  N10: IC1.Enable_2, Composants1.D11_PWM/MOSI
  N11: IC1.In_3, Composants1.A3
  N12: IC1.Out_3_(_Controlled_by_Enable_2_), M2.pin_2
  N13: IC1.Out_4_(_Controlled_by_Enable_2_), M2.pin_1
  N14: IC1.In_4, Composants1.A2
  N15: LED1.anode, Composants1.D13/SCK
  N16: SERVO.pin3, Composants1.D8
  Test accus: Composants1.A4, R5.Pin_1, R6.Pin_0
  N17: Composants1.A1, R4.Pin_0
  N18: Composants1.A0, R1.Pin_0, R2.Pin_0, R3.Pin_0
  HS: Composants1.D10_PWM/SS, Composants1.D9_PWM
  N19: Jump.pin1, Jump.pin2
  N20: Accus_2S.pin1, BAT_2S.-
  N21: Accus_2S.pin2, BAT_2S.+
  N22: R1.Pin_1, LED2.anode
  N23: R2.Pin_1, LED3.anode
  N24: R3.Pin_1, LED4.anode
  N25: R4.Pin_1, LED5.anode
